# Fritzing sketch TrafficScheme (saved by Fritzing 0.9.3b)
breadboards: 2

parts:
  LED1 = LED - 5mm [color="White (4500K)" package="5 mm [THT]"]
  LED2 = LED - 5mm [color="Red (633nm)" package="5 mm [THT]"]
  LED3 = smd LED [color="Green (565nm)" package="0603 [SMD]"]
  LED4 = LED - 5mm [color="Red (633nm)" package="5 mm [THT]"]
  LED5 = LED - 5mm [color="Yellow (585nm)" package="5 mm [THT]"]
  LED6 = LED - 5mm [color="Green (560nm)" package="5 mm [THT]"]
  J1 = Piezo Speaker
  S1 = Pushbutton [package="[THT]"]
  R1 = Resistor [tolerance=±5% resistance=330 package=THT]
  R2 = Resistor [tolerance=±5% resistance=330 package=THT]
  R3 = Resistor [tolerance=±5% resistance=330 package=THT]
  R4 = Resistor [tolerance=±5% resistance=330 package=THT]
  R5 = Resistor [tolerance=±5% resistance=330 package=THT]
  R6 = Resistor [tolerance=±5% resistance=330 package=THT]
  R7 = Resistor [tolerance=±5% resistance=330 package=THT]
  R8 = Resistor [tolerance=±5% resistance=10k package=THT]
  Componente1 = Arduino Uno (Rev3)

nets:
  N1: LED1.cathode, R1.Pin_1
  N2: LED1.anode, Componente1.D11_PWM/MOSI
  N3: LED2.cathode, R7.Pin_1
  N4: LED2.anode, Componente1.D2
  N5: LED3.cathode, R6.Pin_1
  N6: LED3.anode, Componente1.D3_PWM
  N7: LED4.cathode, R4.Pin_1
  N8: LED4.anode, Componente1.D10_PWM/SS
  N9: LED5.cathode, R3.Pin_1
  N10: LED5.anode, Componente1.D9_PWM
  N11: LED6.cathode, R2.Pin_1
  N12: LED6.anode, Componente1.D8
  N13: J1.pin1, R5.Pin_1
  N14: J1.pin2, Componente1.D4
  N15: S1.Pin_1, Componente1.5V
  N16: S1.Pin_3, S1.Pin_4, Componente1.D7
  N17: R1.Pin_0, R2.Pin_0, R3.Pin_0, R4.Pin_0, R5.Pin_0, R6.Pin_0, R7.Pin_0, R8.Pin_0, Componente1.GND
